# Fritzing sketch circuit (saved by Fritzing 0.9.3b)
breadboards: 1

parts:
  Part1 = Arduino Uno (Rev3) - ICSP
  PIR1 = PIR sensor
  Mod1 = KY-019 5V Relay Module [package="Breakout board"]
  BULB1 = Incandescent light bulb small [package="bulb sm"]

nets:
  N1: Part1.D8, PIR1.SIG
  GND: Part1.GND, PIR1.GND, Mod1.-
  N2: Part1.D7, Mod1.S
  5V: Part1.5V, PIR1.VDD, Mod1.+
  N3: Mod1.Common, BULB1.1

custom parts:
  KY-019 5V Relay Module: KY-019 5V Relay module, used to control AC circuits. (Special thanks to vanepp for fixing the PCB holes and other errors)
